// Logisim project ZCS_4.circ as structural Verilog: 2 circuits, main circuit main
module main (
);

  REG_Y reg_y_1 ();  // open: IN0, IN1, IN2, IN3, WE, CLK, IR, OUT0, OUT1, OUT2, OUT3
endmodule

module REG_Y (
  input  IN0,
  input  IN1,
  input  IN2,
  input  IN3,
  input  WE,
  input  CLK,
  input  IR,
  output OUT0,
  output OUT1,
  output OUT2,
  output OUT3
);

  Register #(.width(4)) register_1 (
    .D({IN3, IN2, IN1, IN0}), .en(WE), .clk(CLK), .Q({OUT3, OUT2, OUT1, OUT0}), .clr(IR));
endmodule
